# Fritzing sketch Esqumatico_Carrito (saved by Fritzing 0.9.8b)

parts:
  Componente1 = Arduino Uno (Rev3) - ICSP
  Mod1 = KY-022 Infrared Receiver Module [package="Breakout board"]
  M1 = gear-motor
  M2 = gear-motor
  M3 = gear-motor
  M4 = gear-motor
  S1 = H-Bridge with L298N
  VCC1 = Battery
  VCC2 = Battery block 9V

nets:
  N1: Componente1.D8, S1.IN4
  N2: Componente1.D11_PWM/MOSI, Mod1.S
  N3: Componente1.D5_PWM, S1.IN1
  N4: Componente1.D6_PWM, S1.IN2
  N5: Componente1.D7, S1.IN3
  N6: Componente1.5V, Mod1.-
  GND: Componente1.GND, Mod1.Vin, S1.GND, VCC1.-, VCC2.-
  N7: Componente1.VIN, VCC2.+
  N8: M1.pin_1, M2.pin_2, S1.M1-02
  N9: M1.pin_2, M2.pin_1, S1.M1-01
  N10: M3.pin_1, M4.pin_2, S1.M2-01
  N11: M3.pin_2, M4.pin_1, S1.M2-02
  N12: S1.12V, VCC1.+
  N13: S1.ENA, S1.ENA-5V
  N14: S1.ENB, S1.ENB-5V

custom parts:
  KY-022 Infrared Receiver Module: KY-022 IR receiver module, reacts to 38kHz infrared light.
  H-Bridge with L298N: h-bridge
