# Fritzing sketch Esqumatico_Decoder (saved by Fritzing 0.9.8b)

parts:
  Componente1 = Arduino Uno (Rev3) - ICSP
  Mod1 = KY-022 Infrared Receiver Module [package="Breakout board"]

nets:
  N1: Componente1.D11_PWM/MOSI, Mod1.S
  N2: Componente1.5V, Mod1.-
  GND: Componente1.GND, Mod1.Vin

custom parts:
  KY-022 Infrared Receiver Module: KY-022 IR receiver module, reacts to 38kHz infrared light.
